// Logisim project pipelined2.circ as structural Verilog: 12 circuits, main circuit main
module ALU_control (
  input  [1:0] ALUop,
  input  [5:0] Funct,
  input  [2:0] IMM_OP,
  output [3:0] Output
);

  PLA #(.in_width(11), .out_width(4), .truth_table("00xxxxxxxxx,0010#lw/sw\n01xxxxxxxxx,0110#beq/bne\n10xxx100001,0010#addu\n10xxx100011,0110#subu\n10xxx100100,0000#AND\n10xxx100101,0001#OR\n10xxx100111,1100#nor\n10xxx101010,0111#slt\n11001xxxxxx,0010#addiu\n11010xxxxxx,0111#slti\n11100xxxxxx,0000#andi\n11101xxxxxx,0001#ori\n10xxx000010,0010#jr\n10xxx000011,0010#jral")) pla_1 (.out(Output));  // open: in
endmodule

module Bit_extender (
  input  [15:0] Input,
  input  Signed,
  output [31:0] Output
);

  wire and_1_out;

  Multiplexer #(.width(16)) multiplexer_1 (.in0({16{1'b0}}), .in1({16{1'b1}}), .out(Output[31:16]), .sel(and_1_out));
  and and_1 (and_1_out, Input[15], Signed);

  assign Output[15:0] = Input;
endmodule

module main (
);

  wire ClearPipe, Clock, control_1_signedimm, EX_MemRead, MEM_MemRead, MEM_MemWrite, MEM_RegWrite, MEM_Zero,
       mips_alu_1_p4, Stall, WB_RegWrite;
  wire [1:0] control_1_memory, control_1_registerwritesrc, ex_mem_1_registerwritesrc_2, ForwardA, ForwardB,
       id_ex_1_registerwritesrc_2, mem_wb_1_registerwritesrc_2;
  wire [1:1] id_ex_1_memory_2;
  wire [2:0] control_1_alu, control_1_branching, control_1_register, EX_ALU, EX_Register,
       id_ex_1_branching_2, MEM_Branching;
  wire [3:0] mips_alu_1_p3;
  wire [4:0] EX_RegDst, EX_RegisterRs, EX_RegisterRt, MEM_RegDst, WB_RegDst;
  wire [27:0] EX_PC;
  wire [31:0] bit_extender_1_output, EX_BranchPC, EX_Data1, EX_Data2, EX_IMM, EX_WriteData, ID_OP, ID_PC,
       MEM_AluResult, MEM_BranchPC, MEM_jalPC, MEM_JumpPC, MEM_MemoryResult, mem_wb_1_aluresult_2,
       mem_wb_1_jalpc_2, mem_wb_1_memoryresult_2, MEM_WriteData, mips_alu_1_p2, mips_alu_1_p5,
       mipsprogramrom_1_p2, multiplexer_3_out, NewPC, pc_1_nextpc, pc_1_pc, registerfile_1_p7,
       registerfile_1_p8, shifter_1_out, WB_Result;
  wire [31:2] EX_JumpPC;
  wire [31:26] EX_OP;

  Branch_Control branch_control_1 (
    .Clear(ClearPipe), .NewPC(NewPC), .Zero(MEM_Zero), .Branching(MEM_Branching), .BranchPC(MEM_BranchPC),
    .JumpPC(MEM_JumpPC), .AluResult(MEM_AluResult));
  PC pc_1 (.PC(pc_1_pc), .NewPC(NewPC), .Clear(ClearPipe), .Stall(Stall), .Clock(Clock), .NextPC(pc_1_nextpc));
  // MIPSProgramROM mipsprogramrom_1: pin names not known; wires that end beside it: pc_1_pc, mipsprogramrom_1_p2
  IF_ID if_id_1 (
    .PC(pc_1_nextpc), .OP(mipsprogramrom_1_p2), .ClearPipe(ClearPipe), .Stall(Stall), .Clock(Clock),
    .PC_2(ID_PC), .OP_2(ID_OP));
  Clock clock_1 (.out(Clock));
  Forwarding_unit forwarding_unit_1 (
    .EX_RegisterRt(EX_RegisterRt), .MEM_RegisterRd(MEM_RegDst), .WB_RegisterRd(WB_RegDst),
    .EX_RegisterRs(EX_RegisterRs), .WB_RegWrite(WB_RegWrite), .MEM_RegWrite(MEM_RegWrite),
    .ForwardA(ForwardA), .ForwardB(ForwardB));
  Hazard_detection_unit hazard_detection_unit_1 (
    .EX_MemRead(EX_MemRead), .EX_RegDst(EX_RegDst), .ID_RegisterRt(ID_OP[25:21]),
    .ID_RegisterRs(ID_OP[20:16]), .EX_AluInput(EX_ALU[0]), .Stall(Stall));
  Bit_extender bit_extender_1 (.Input(ID_OP[15:0]), .Signed(control_1_signedimm), .Output(bit_extender_1_output));
  Control control_1 (
    .Funct(ID_OP[5:0]), .OP(ID_OP[31:26]), .SignedIMM(control_1_signedimm), .Alu(control_1_alu),
    .Branching(control_1_branching), .Memory(control_1_memory),
    .RegisterWriteSrc(control_1_registerwritesrc), .Register(control_1_register));
  // RegisterFile #(.trigger("falling")) registerfile_1: pin names not known; wires that end beside it: WB_Result, Clock, WB_RegWrite, WB_RegDst, ID_OP[25:21], ID_OP[20:16], registerfile_1_p7, registerfile_1_p8
  ID_EX id_ex_1 (
    .Data1(registerfile_1_p7), .Data2(registerfile_1_p8), .RegisterRt(ID_OP[25:21]),
    .RegisterRs(ID_OP[20:16]), .OP(ID_OP), .PC(ID_PC), .IMM(bit_extender_1_output), .ALU(control_1_alu),
    .Branching(control_1_branching), .Memory(control_1_memory),
    .RegisterWriteSrc(control_1_registerwritesrc), .Register(control_1_register), .ClearPipe(ClearPipe),
    .Stall(Stall), .Clock(Clock), .Data1_2(EX_Data1), .Data2_2(EX_Data2), .RegisterRt_2(EX_RegisterRt),
    .RegisterRs_2(EX_RegisterRs), .OP_2({EX_OP, EX_JumpPC[27:2]}), .PC_2({EX_JumpPC[31:28], EX_PC}),
    .IMM_2(EX_IMM), .ALU_2(EX_ALU), .Branching_2(id_ex_1_branching_2),
    .Memory_2({id_ex_1_memory_2[1], EX_MemRead}), .RegisterWriteSrc_2(id_ex_1_registerwritesrc_2),
    .Register_2(EX_Register));
  Multiplexer #(.select(2), .width(32)) multiplexer_1 (
    .in0(EX_Data2), .in1(WB_Result), .in2(MEM_AluResult), .in3(MEM_AluResult), .out(EX_WriteData),
    .sel(ForwardB));
  Multiplexer #(.select(2), .width(5)) multiplexer_2 (
    .in0(EX_JumpPC[22:18]), .in1(EX_JumpPC[17:13]), .in2({5{1'b1}}), .out(EX_RegDst), .sel(EX_Register[1:0]));  // open: in3
  Multiplexer #(.select(2), .width(32)) multiplexer_3 (
    .in0(EX_Data1), .in1(WB_Result), .in2(MEM_AluResult), .in3(MEM_AluResult), .out(multiplexer_3_out),
    .sel(ForwardA));
  Shifter #(.width(32)) shifter_1 (.in(EX_IMM), .\dist (5'b00010), .out(shifter_1_out));
  // Mips_ALU mips_alu_1: pin names not known; wires that end beside it: multiplexer_3_out, mips_alu_1_p2, mips_alu_1_p3, mips_alu_1_p4, mips_alu_1_p5
  Multiplexer #(.width(32)) multiplexer_4 (.in0(EX_IMM), .in1(EX_WriteData), .out(mips_alu_1_p2), .sel(EX_ALU[0]));
  Adder #(.width(32)) adder_1 (.a(shifter_1_out), .b({EX_JumpPC[31:28], EX_PC}), .out(EX_BranchPC));  // open: cin, cout
  ALU_control alu_control_1 (
    .Output(mips_alu_1_p3), .ALUop(EX_ALU[2:1]), .Funct(EX_JumpPC[7:2]), .IMM_OP(EX_OP[28:26]));
  EX_MEM ex_mem_1 (
    .Zero(mips_alu_1_p4), .AluResult(mips_alu_1_p5), .WriteData(EX_WriteData), .BranchPC(EX_BranchPC),
    .JumpPC({EX_JumpPC, 2'b00}), .jalPC({EX_JumpPC[31:28], EX_PC}), .RegDst(EX_RegDst),
    .Branching(id_ex_1_branching_2), .Memory({id_ex_1_memory_2[1], EX_MemRead}),
    .RegisterWriteSrc(id_ex_1_registerwritesrc_2), .RegWrite(EX_Register[2]), .ClearPipe(ClearPipe),
    .Clock(Clock), .Zero_2(MEM_Zero), .AluResult_2(MEM_AluResult), .WriteData_2(MEM_WriteData),
    .BranchPC_2(MEM_BranchPC), .JumpPC_2(MEM_JumpPC), .jalPC_2(MEM_jalPC), .RegDst_2(MEM_RegDst),
    .Branching_2(MEM_Branching), .Memory_2({MEM_MemWrite, MEM_MemRead}),
    .RegisterWriteSrc_2(ex_mem_1_registerwritesrc_2), .RegWrite_2(MEM_RegWrite));
  // MIPS_RAM #(.addrWidth(24)) mips_ram_1: pin names not known; wires that end beside it: MEM_AluResult[23:0], MEM_WriteData, MEM_MemWrite, MEM_MemRead, Clock, MEM_MemoryResult
  MEM_WB mem_wb_1 (
    .MemoryResult(MEM_MemoryResult), .AluResult(MEM_AluResult), .jalPC(MEM_jalPC), .RegDst(MEM_RegDst),
    .RegisterWriteSrc(ex_mem_1_registerwritesrc_2), .RegWrite(MEM_RegWrite), .Clock(Clock),
    .MemoryResult_2(mem_wb_1_memoryresult_2), .AluResult_2(mem_wb_1_aluresult_2), .jalPC_2(mem_wb_1_jalpc_2),
    .RegDst_2(WB_RegDst), .RegisterWriteSrc_2(mem_wb_1_registerwritesrc_2), .RegWrite_2(WB_RegWrite));
  Multiplexer #(.select(2), .width(32)) multiplexer_5 (
    .in0(mem_wb_1_aluresult_2), .in1(mem_wb_1_memoryresult_2), .in2(mem_wb_1_jalpc_2), .out(WB_Result),
    .sel(mem_wb_1_registerwritesrc_2));  // open: in3

  // Other names for the same wires on the sheet: EX_AluInput = EX_ALU[0]; EX_OP[25:0] = EX_JumpPC[27:2];
  //   EX_PC[31:28] = EX_JumpPC[31:28]; EX_RegWrite = EX_Register[2]; ID_RegisterRs[4:0] = ID_OP[20:16];
  //   ID_RegisterRt[4:0] = ID_OP[25:21]

  // Notes on the sheet:
  //   contents of mipsprogramrom_1 (hex, n*v repeats v):
  //   ori     $sp, $zero, 0                   # initialize stack to  the whole memory.
  //   # When you push something to the stack                                             # it will be put
  //   at the largest possible address)     jal     main                            # call main init_loop:
  //   j       init_loop                       # infinite loop  mul:     ori     $v0, $zero, 0
  //   # res = 0 mul_loop_init:     slt     $a2, $zero, $a0                 # b > 0?     beq     $a2,
  //   $zero, mul_exit            # if(b > 0) goto mul_exit mul_loop:     addu    $v0, $v0, $a0
  //   # res += a     addiu   $a1, $a1, -1                    # b--     bne     $a1, $zero, mul_loop
  //   # if(b != 0) goto mul_loop mul_exit:     jr      $ra                             # return
  //   largest_prime: # int largest_prime(int n) # Finds largest prime less than n using the Sieve of
  //   Eratosthenes     addiu   $sp, $sp, -16                   # make room to save 4 32-bit words     sw
  //   $s2, 12($sp)                    # save $s2 on stack, $s2 = p     sw      $s1, 8($sp)
  //   # save $s1 on stack, $s1 = i     sw      $s0, 4($sp)                     # save $s0 on stack, $s0 =
  //   n     sw      $ra, 0($sp)                     # save return address     ori     $s0, $a0, 0
  //   # save n in $s0      addu    $t0, $s0, $s0                   # adjust stack pointer to     addu
  //   $t0, $t0, $t0                   # make room for primes array     subu    $sp, $sp, $t0
  //   slti    $t0, $s0, 3                     # n <= 2?     bne     $t0, $zero, lp_return_zero      # if(n
  //   <= 2) return 0  # Loop 1, set primes[i] = i, for 2 <= i < n     ori     $s1, $zero, 2
  //   # i = 2 lp_loop1:     addu    $t0, $s1, $s1                   # Address for primes[i]     addu
  //   $t0, $t0, $t0                   # Address for primes[i]     addu    $t0, $t0, $sp
  //   # Address for primes[i]     sw      $s1, 0($t0)                     # primes[i] = i     addiu   $s1,
  //   $s1, 1                     # i += 1     bne     $s0, $s1, lp_loop1              # if(n != 0) goto
  //   lp_loop1  # Loop 2, goes through array, looking for primes p. # When it finds them, marks
  //   multiplications of p as not-prime     ori     $s2, $zero, 1                   # Start at p=2
  //   (increased in a sec) lp_loop2:     addiu   $s2, $s2, 1                     # p++     ori     $a0,
  //   $s2, 0                     # set param, p     ori     $a1, $s2, 0                     # set param, p
  //   jal     mul                             # call mul(p,p)     slt     $t0, $v0, $s0
  //   # mul(p,p) < n     beq     $t0, $zero, lp_loop2_end        # if(mul(p,p) < n) exit loop 2      addu
  //   $t0, $s2, $s2                   # Address for primes[p]     addu    $t0, $t0, $t0
  //   # Address for primes[p]     addu    $t0, $t0, $sp                   # Address for primes[p]     lw
  //   $t0, 0($t0)                     # Load primes[p]     ori     $s1, $zero, 2                   # i =
  //   2, in this order to avoid blocking     beq     $t0, $zero, lp_loop2            # primes[0] == 0,
  //   loop again lp_loop2_1:     ori     $a0, $s1, 0                     # set param, i     ori     $a1,
  //   $s2, 0                     # set param, p     jal     mul                             # call idx =
  //   mul(i,p)     slt     $t0, $v0, $s0                   # idx < n?     beq     $t0, $zero, lp_loop2
  //   # if (idx>=n) exit inner loop     addu    $t0, $v0, $v0                   # Address for primes[idx]
  //   addu    $t0, $t0, $t0                   # Address for primes[idx]     addu    $t0, $t0, $sp
  //   # Address for primes[idx]     sw      $zero, 0($t0)                   # primes[idx] = 0     addiu
  //   $s1, $s1, 1                     # i++     j       lp_loop2_1                      # inner loop
  //   lp_loop2_end:  # Loop 3 starts at primes[n-1] and continues down until a prime is found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
endmodule

module Control (
  input  [5:0] Funct,
  input  [5:0] OP,
  output SignedIMM,
  output [2:0] Alu,
  output [2:0] Branching,
  output [1:0] Memory,
  output [1:0] RegisterWriteSrc,
  output [2:0] Register
);

  PLA #(.in_width(6), .truth_table("001000,10#jr\n001001,11#jral")) jr_jral ();  // open: in, out
  PLA #(.in_width(8), .out_width(14), .truth_table("00000000,10100000001010#R-format\n000100xx,00000001000111#beq\n000101xx,00000001010111#bne\n001001xx,10000000001101#addiu\n001010xx,10000000001101#slti\n001100xx,10000000001100#andi\n001101xx,10000000001100#ori\n100011xx,10001010000001#lw\n101011xx,00000100000001#sw\n000010xx,00000001100010#j\n000011xx,11010001100010#jal\n00000010,00000001110010#jr\n00000011,11010001110010#jral")) pla_1 (.out(Memory));  // open: in
endmodule

module Forwarding_unit (
  input  WB_RegWrite,
  input  MEM_RegWrite,
  input  [4:0] EX_RegisterRt,
  input  [4:0] MEM_RegisterRd,
  input  [4:0] WB_RegisterRd,
  input  [4:0] EX_RegisterRs,
  output [1:0] ForwardA,
  output [1:0] ForwardB
);

  wire comparator_1_eq, comparator_2_eq, comparator_3_eq, comparator_4_eq;

  Comparator #(.width(5), .mode("unsigned")) comparator_1 (
    .a(EX_RegisterRt), .b(MEM_RegisterRd), .eq(comparator_1_eq));  // open: gt, lt
  Comparator #(.width(5), .mode("unsigned")) comparator_2 (
    .a(EX_RegisterRt), .b(WB_RegisterRd), .eq(comparator_2_eq));  // open: gt, lt
  Comparator #(.width(5), .mode("unsigned")) comparator_3 (
    .a(EX_RegisterRs), .b(MEM_RegisterRd), .eq(comparator_3_eq));  // open: gt, lt
  Comparator #(.width(5), .mode("unsigned")) comparator_4 (
    .a(EX_RegisterRs), .b(WB_RegisterRd), .eq(comparator_4_eq));  // open: gt, lt
  and and_1 (ForwardA[0], comparator_2_eq, WB_RegWrite);
  and and_2 (ForwardB[0], comparator_4_eq, WB_RegWrite);
  and and_3 (ForwardA[1], MEM_RegWrite, comparator_1_eq);
  and and_4 (ForwardB[1], MEM_RegWrite, comparator_3_eq);
endmodule

module Hazard_detection_unit (
  input  EX_MemRead,
  input  [4:0] EX_RegDst,
  input  [4:0] ID_RegisterRt,
  input  [4:0] ID_RegisterRs,
  input  EX_AluInput,
  output Stall
);

  wire and_1_out, and_3_out, comparator_1_eq, comparator_2_eq, comparator_3_eq, or_1_out;

  Comparator #(.width(5), .mode("unsigned")) comparator_1 (
    .a({5{1'b0}}), .b(EX_RegDst), .eq(comparator_1_eq));  // open: gt, lt
  Comparator #(.width(5), .mode("unsigned")) comparator_2 (
    .a(EX_RegDst), .b(ID_RegisterRt), .eq(comparator_2_eq));  // open: gt, lt
  Comparator #(.width(5), .mode("unsigned")) comparator_3 (
    .a(EX_RegDst), .b(ID_RegisterRs), .eq(comparator_3_eq));  // open: gt, lt
  and and_1 (and_1_out, comparator_3_eq, EX_AluInput);
  or or_1 (or_1_out, comparator_2_eq, and_1_out);
  and and_2 (Stall, EX_MemRead, and_3_out);
  and and_3 (and_3_out, ~comparator_1_eq, or_1_out);  // AND_Gate
endmodule

module ID_EX (
  input  [31:0] Data1,
  input  [31:0] Data2,
  input  [4:0] RegisterRt,
  input  [4:0] RegisterRs,
  input  [31:0] OP,
  input  [31:0] PC,
  input  [31:0] IMM,
  input  [2:0] ALU,
  input  [2:0] Branching,
  input  [1:0] Memory,
  input  [1:0] RegisterWriteSrc,
  input  [2:0] Register,
  input  ClearPipe,
  input  Stall,
  input  Clock,
  output [31:0] Data1_2,
  output [31:0] Data2_2,
  output [4:0] RegisterRt_2,
  output [4:0] RegisterRs_2,
  output [31:0] OP_2,
  output [31:0] PC_2,
  output [31:0] IMM_2,
  output [2:0] ALU_2,
  output [2:0] Branching_2,
  output [1:0] Memory_2,
  output [1:0] RegisterWriteSrc_2,
  output [2:0] Register_2
);

  wire or_1_out;
  wire [1:0] multiplexer_2_out;
  wire [2:0] multiplexer_1_out, multiplexer_3_out;

  Multiplexer #(.width(3)) multiplexer_1 (.in0(Branching), .in1(3'b000), .out(multiplexer_1_out), .sel(or_1_out));
  Multiplexer #(.width(2)) multiplexer_2 (.in0(Memory), .in1(2'b00), .out(multiplexer_2_out), .sel(or_1_out));
  Multiplexer #(.width(3)) multiplexer_3 (.in0(Register), .in1(3'b000), .out(multiplexer_3_out), .sel(or_1_out));
  or or_1 (or_1_out, ClearPipe, Stall);
  Register #(.width(32)) u_Data1 (.D(Data1), .en(1'b1), .Q(Data1_2), .clk(Clock));  // open: clr
  Register #(.width(32)) u_Data2 (.D(Data2), .en(1'b1), .Q(Data2_2), .clk(Clock));  // open: clr
  Register #(.width(5)) u_RegisterRt (.D(RegisterRt), .en(1'b1), .Q(RegisterRt_2), .clk(Clock));  // open: clr
  Register #(.width(5)) u_RegisterRs (.D(RegisterRs), .en(1'b1), .Q(RegisterRs_2), .clk(Clock));  // open: clr
  Register #(.width(32)) u_OP (.D(OP), .en(1'b1), .Q(OP_2), .clk(Clock));  // open: clr
  Register #(.width(32)) u_PC (.D(PC), .en(1'b1), .Q(PC_2), .clk(Clock));  // open: clr
  Register #(.width(32)) u_IMM (.D(IMM), .en(1'b1), .Q(IMM_2), .clk(Clock));  // open: clr
  Register #(.width(3)) u_ALU (.D(ALU), .en(1'b1), .Q(ALU_2), .clk(Clock));  // open: clr
  Register #(.width(3)) u_Branching (.D(multiplexer_1_out), .en(1'b1), .Q(Branching_2), .clk(Clock));  // open: clr
  Register #(.width(2)) u_Memory (.D(multiplexer_2_out), .en(1'b1), .Q(Memory_2), .clk(Clock));  // open: clr
  Register #(.width(2)) u_RegisterWriteSrc (
    .D(RegisterWriteSrc), .en(1'b1), .Q(RegisterWriteSrc_2), .clk(Clock));  // open: clr
  Register #(.width(3)) u_Register (.D(multiplexer_3_out), .en(1'b1), .Q(Register_2), .clk(Clock));  // open: clr
endmodule

module EX_MEM (
  input  Zero,
  input  [31:0] AluResult,
  input  [31:0] WriteData,
  input  [31:0] BranchPC,
  input  [31:0] JumpPC,
  input  [31:0] jalPC,
  input  [4:0] RegDst,
  input  [2:0] Branching,
  input  [1:0] Memory,
  input  [1:0] RegisterWriteSrc,
  input  RegWrite,
  input  ClearPipe,
  input  Clock,
  output Zero_2,
  output [31:0] AluResult_2,
  output [31:0] WriteData_2,
  output [31:0] BranchPC_2,
  output [31:0] JumpPC_2,
  output [31:0] jalPC_2,
  output [4:0] RegDst_2,
  output [2:0] Branching_2,
  output [1:0] Memory_2,
  output [1:0] RegisterWriteSrc_2,
  output RegWrite_2
);

  wire multiplexer_3_out;
  wire [1:0] multiplexer_2_out;
  wire [2:0] multiplexer_1_out;

  Multiplexer #(.width(3)) multiplexer_1 (.in0(Branching), .in1(3'b000), .out(multiplexer_1_out), .sel(ClearPipe));
  Multiplexer #(.width(2)) multiplexer_2 (.in0(Memory), .in1(2'b00), .out(multiplexer_2_out), .sel(ClearPipe));
  Multiplexer multiplexer_3 (.in0(RegWrite), .in1(1'b0), .out(multiplexer_3_out), .sel(ClearPipe));
  Register #(.width(1)) u_Zero (.D(Zero), .en(1'b1), .Q(Zero_2), .clk(Clock));  // open: clr
  Register #(.width(32)) u_AluResult (.D(AluResult), .en(1'b1), .Q(AluResult_2), .clk(Clock));  // open: clr
  Register #(.width(32)) u_WriteData (.D(WriteData), .en(1'b1), .Q(WriteData_2), .clk(Clock));  // open: clr
  Register #(.width(32)) u_BranchPC (.D(BranchPC), .en(1'b1), .Q(BranchPC_2), .clk(Clock));  // open: clr
  Register #(.width(32)) u_JumpPC (.D(JumpPC), .en(1'b1), .Q(JumpPC_2), .clk(Clock));  // open: clr
  Register #(.width(32)) u_jalPC (.D(jalPC), .en(1'b1), .Q(jalPC_2), .clk(Clock));  // open: clr
  Register #(.width(5)) u_RegDst (.D(RegDst), .en(1'b1), .Q(RegDst_2), .clk(Clock));  // open: clr
  Register #(.width(3)) u_Branching (.D(multiplexer_1_out), .en(1'b1), .Q(Branching_2), .clk(Clock));  // open: clr
  Register #(.width(2)) u_Memory (.D(multiplexer_2_out), .en(1'b1), .Q(Memory_2), .clk(Clock));  // open: clr
  Register #(.width(2)) u_RegisterWriteSrc (
    .D(RegisterWriteSrc), .en(1'b1), .Q(RegisterWriteSrc_2), .clk(Clock));  // open: clr
  Register #(.width(1)) u_RegWrite (.D(multiplexer_3_out), .en(1'b1), .Q(RegWrite_2), .clk(Clock));  // open: clr
endmodule

module MEM_WB (
  input  [31:0] MemoryResult,
  input  [31:0] AluResult,
  input  [31:0] jalPC,
  input  [4:0] RegDst,
  input  [1:0] RegisterWriteSrc,
  input  RegWrite,
  input  Clock,
  output [31:0] MemoryResult_2,
  output [31:0] AluResult_2,
  output [31:0] jalPC_2,
  output [4:0] RegDst_2,
  output [1:0] RegisterWriteSrc_2,
  output RegWrite_2
);

  Register #(.width(32)) u_MemoryResult (.D(MemoryResult), .en(1'b1), .Q(MemoryResult_2), .clk(Clock));  // open: clr
  Register #(.width(32)) u_AluResult (.D(AluResult), .en(1'b1), .Q(AluResult_2), .clk(Clock));  // open: clr
  Register #(.width(32)) u_jalPC (.D(jalPC), .en(1'b1), .Q(jalPC_2), .clk(Clock));  // open: clr
  Register #(.width(5)) u_RegDst (.D(RegDst), .en(1'b1), .Q(RegDst_2), .clk(Clock));  // open: clr
  Register #(.width(2)) u_RegisterWriteSrc (
    .D(RegisterWriteSrc), .en(1'b1), .Q(RegisterWriteSrc_2), .clk(Clock));  // open: clr
  Register #(.width(1)) RegisterWrite (.D(RegWrite), .en(1'b1), .Q(RegWrite_2), .clk(Clock));  // open: clr
endmodule

module IF_ID (
  input  [31:0] PC,
  input  [31:0] OP,
  input  ClearPipe,
  input  Stall,
  input  Clock,
  output [31:0] PC_2,
  output [31:0] OP_2
);

  wire or_1_out;
  wire [31:0] multiplexer_1_out;

  Multiplexer #(.width(32)) multiplexer_1 (.in0(OP), .in1({32{1'b0}}), .out(multiplexer_1_out), .sel(ClearPipe));
  or or_1 (or_1_out, ClearPipe, ~Stall);  // OR_Gate
  Register #(.width(32)) u_PC (.D(PC), .en(1'b1), .Q(PC_2), .clk(Clock));  // open: clr
  Register #(.width(32)) u_OP (.D(multiplexer_1_out), .en(or_1_out), .Q(OP_2), .clk(Clock));  // open: clr
endmodule

module PC (
  input  Clear,
  input  [31:0] NewPC,
  input  Stall,
  input  Clock,
  output [31:0] NextPC,
  output [31:0] PC
);

  wire or_1_out;
  wire [31:0] multiplexer_1_out;

  Multiplexer #(.width(32)) multiplexer_1 (.in0(NextPC), .in1(NewPC), .out(multiplexer_1_out), .sel(Clear));
  or or_1 (or_1_out, Clear, ~Stall);  // OR_Gate
  Register #(.width(32)) u_PC (.D(multiplexer_1_out), .en(or_1_out), .Q(PC), .clk(Clock));  // open: clr
  Adder #(.width(32)) adder_1 (.a(PC), .b(32'h4), .out(NextPC));  // open: cin, cout
endmodule

module Branch_Control (
  input  Zero,
  input  [2:0] Branching,
  input  [31:0] BranchPC,
  input  [31:0] JumpPC,
  input  [31:0] AluResult,
  output Clear,
  output [31:0] NewPC
);

  wire or_1_out, xor_1_out;

  and and_1 (Clear, or_1_out, Branching[2]);
  or or_1 (or_1_out, xor_1_out, Branching[1]);
  xor xor_1 (xor_1_out, Zero, Branching[0]);
  Multiplexer #(.select(2), .width(32)) multiplexer_1 (
    .in0(BranchPC), .in1(BranchPC), .in2(JumpPC), .in3(AluResult), .out(NewPC), .sel(Branching[1:0]));
endmodule
